# Fritzing sketch FRITZING LightMeter2020-Chloe (saved by Fritzing 0.9.4)
breadboards: 1

parts:
  Part1 = Arduino Uno (Rev3)
  LED1 = LED - 5mm [color="Red (633nm)" package="5 mm [THT]"]
  LED2 = LED - 5mm [color="Yellow (595nm)" package="5 mm [THT]"]
  LED3 = LED - 5mm [color="Green (570nm)" package="5 mm [THT]"]
  LED4 = LED - 5mm [color="White (4500K)" package="5 mm [THT]"]
  R1 = Resistor [tolerance=±5% resistance=100 package=THT]
  R2 = Resistor [tolerance=±5% resistance=100 package=THT]
  R3 = Resistor [tolerance=±5% resistance=100 package=THT]
  R4 = Resistor [tolerance=±5% resistance=100 package=THT]
  R5 = Photocell (LDR) [package=THT]
  R6 = Resistor [tolerance=±5% resistance=1k package=THT]

nets:
  N1: Part1.A0, Part1.GND, LED1.anode, LED2.anode, LED3.anode, LED4.anode, R5.pin_1, R6.Pin_0
  N2: Part1.D9_PWM, R4.Pin_0
  N3: Part1.D3_PWM, R1.Pin_0
  N4: Part1.D5_PWM, R2.Pin_0
  N5: Part1.D6_PWM, R3.Pin_0
  N6: Part1.5V, R5.pin_0
  N7: LED1.cathode, R4.Pin_1
  N8: LED2.cathode, R3.Pin_1
  N9: LED3.cathode, R2.Pin_1
  N10: LED4.cathode, R1.Pin_1

notes:
  To bring power to the other side of the Breadboard
  Individual Circuits for each LED, Connected to Pins 3,5,6,9
  Photoresistor connected to A0 (Analog Input)
  1K Resistor used for Photoresistor

// code stored in the sketch: Lab 3:4 -Chloe dunwoody -Unknown.ino
#define LED1 
#define LED2 
#define LED3 
#define LED4 
#define lightSensor A0


void setup() {
Serial.begin(9600);

 
}

void loop() {
 int lightIntensity = analogRead(lightSensor);
 Serial.println(lightIntensity);
 delay(100);


}
